# Fritzing sketch arduino-interupt-encoder (saved by Fritzing 0.9.2b)
breadboards: 1

parts:
  RE1 = Rotary Encoder [package=THT]
  R1 = Resistor [tolerance=±5% resistance=220 package=THT]
  R2 = Resistor [tolerance=±5% resistance=220 package=THT]
  Bauteil1 = Arduino Uno (Rev3)

nets:
  N1: RE1.EncoderPinA, R2.Pin_1, Bauteil1.D3_PWM
  N2: RE1.EncoderPinC, Bauteil1.GND
  N3: RE1.EncoderPinB, R1.Pin_0, Bauteil1.D2
  N4: R1.Pin_1, R2.Pin_0, Bauteil1.5V
